# Fritzing sketch main (saved by Fritzing 1.0.2b)
breadboards: 1

parts:
  Part1 = SparkFun Motor Driver TB6612FNG (v11) [part_number=ROB-14451]
  M2 = DC Motor [voltage_(max)=6V voltage_(min)=3V]
  VCC1 = Battery block 9V
  M3 = DC Motor [voltage_(max)=6V voltage_(min)=3V]
  S1 = Pushbutton [package="[THT]"]
  R1 = Resistor [tolerance=±5% power=0.25W resistance=220 package=THT]
  LED1 = LED - 5mm [color="Red (633nm)" current=0.030A package="5 mm [THT]"]
  A1 = mini560 [package=THT]
  U1 = ESP32S-HiLetgo [part_number=ESP32S-HiLetgo]

nets:
  GND: Part1.GND, VCC1.-, LED1.cathode, A1.pin_4, A1.pin_6, A1.pin_7, U1.GND
  N1: Part1.B01, M3.pin_2
  N2: Part1.B02, M3.pin_1
  N3: Part1.A02, M2.pin_1
  N4: Part1.A01, M2.pin_2
  N5: Part1.VCC, S1.Pin_3, S1.Pin_4, U1.3.3
  N6: Part1.VM, A1.pin_9, U1.VIN
  N7: Part1.PWMA, U1.GPIO26
  N8: Part1.AIN2, U1.GPIO14
  N9: Part1.AIN1, U1.GPIO13
  N10: Part1.STBY, U1.GPIO33
  N11: Part1.BIN1, U1.GPIO18
  N12: Part1.BIN2, U1.GPIO19
  N13: Part1.PWMB, U1.GPIO23
  N14: VCC1.+, A1.pin_1, A1.pin_2
  N15: S1.Pin_1, S1.Pin_2, U1.GPIO32
  N16: R1.Pin_0, U1.GPIO22
  N17: R1.Pin_1, LED1.anode

custom parts:
  SparkFun Motor Driver TB6612FNG (v11): The TB6612FNG Motor Driver can control up to two DC motors at a constant current of 1.2A (3.2A peak). Two input signals (IN1 and IN2) can be used to control the motor in one of four function modes: CW, CCW, short-brake and stop. The two motor outputs (A and B) can be separately controlled, and the speed of each motor is controlled via a PWM input signal with a frequency up to 100kHz. The STBY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
  mini560: 5A DC-DC Mini 560 Step Down Stabilized Voltage Supply Module Output 3.3 5V 9V 12V Step-down Power Converter Board Module
  ESP32S-HiLetgo: HiLetgo ESP-WROOM-32 ESP32 ESP-32S Development Board 2.4GHz Dual-Mode WiFi + Bluetooth Dual Cores Microcontroller The ESP32 integrated with Antenna switches, RF Balun, power amplifiers, low-noise amplifiers, filters, and management modules, and the entire solution occupies the least area of PCB. 2.4 GHz Wi-Fi plus Bluetooth dual-mode chip, with TSMC Ultra-low power consumption 40nm technology,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
