# Fritzing sketch tema-7_servo (saved by Fritzing 1.0.2b)
breadboards: 1

parts:
  S1 = Pushbutton [package="[SMD]"]
  R1 = Resistor [tolerance=±5% power=0.25W resistance=220 package=THT]
  A1 = ESP32-S3-WROOM-1-N16R8 dev board
  J1 = Basic Servo

nets:
  N1: S1.Pin_1, S1.Pin_2, R1.Pin_0, A1.Pin_9
  N2: S1.Pin_3, S1.Pin_4, A1.Pin_1, A1.Pin_2, J1.vcc
  N3: R1.Pin_1, A1.Pin_23, A1.Pin_44, J1.gnd
  N4: A1.Pin_8, J1.pulse

custom parts:
  ESP32-S3-WROOM-1-N16R8 dev board: ESP32-S3 WIFI+BLE5.0 Development Board ESP32-S3-WROOM-1-N16R8(16M Flash/8SRAM).
